// Logisim project CPU.circ as structural Verilog
module ALU (
  input  enable_del_dmx,
  input  opcode_1,
  input  opcode_2,
  input  opcode3,
  input  opcode_4,
  input  in1,
  input  in2,
  input  in3,
  input  in4,
  input  in5,
  input  in6,
  input  in7,
  input  in8,
  output Overflow,
  output Overflow_2
);

  wire add_1_out_10, add_1_out_11, add_1_out_12, add_1_out_13, and_1_out, and_2_out, and_3_out, and_4_out,
       controlled_buffer_1_out, controlled_buffer_2_out, controlled_buffer_3_out, controlled_buffer_4_out,
       demultiplexer_1_out1, demultiplexer_1_out2, demultiplexer_1_out3, demultiplexer_1_out4,
       demultiplexer_1_out5, demultiplexer_1_out6, not_1_out, or_1_out, or_2_out, or_3_out, or_4_out,
       reloj_out, subs_1_out_10, subs_1_out_11, subs_1_out_12, subs_1_out_13, xor_1_out, xor_2_out,
       xor_3_out, xor_4_out;

  assign controlled_buffer_1_out = demultiplexer_1_out1 ? and_1_out : 1'bz;  // Controlled_Buffer controlled_buffer_1
  and and_1 (and_1_out, in1, in5);
  and and_2 (and_2_out, in2, in6);
  assign controlled_buffer_2_out = demultiplexer_1_out1 ? and_2_out : 1'bz;  // Controlled_Buffer controlled_buffer_2
  assign controlled_buffer_3_out = demultiplexer_1_out1 ? and_3_out : 1'bz;  // Controlled_Buffer controlled_buffer_3
  and and_3 (and_3_out, in3, in7);
  assign controlled_buffer_4_out = demultiplexer_1_out1 ? and_4_out : 1'bz;  // Controlled_Buffer controlled_buffer_4
  and and_4 (and_4_out, in4, in8);
  or or_1 (or_1_out, in1, in5);
  assign controlled_buffer_1_out = demultiplexer_1_out2 ? or_1_out : 1'bz;  // Controlled_Buffer controlled_buffer_5
  or or_2 (or_2_out, in2, in6);
  assign controlled_buffer_2_out = demultiplexer_1_out2 ? or_2_out : 1'bz;  // Controlled_Buffer controlled_buffer_6
  assign controlled_buffer_3_out = demultiplexer_1_out2 ? or_3_out : 1'bz;  // Controlled_Buffer controlled_buffer_7
  or or_3 (or_3_out, in3, in7);
  assign controlled_buffer_4_out = demultiplexer_1_out2 ? or_4_out : 1'bz;  // Controlled_Buffer controlled_buffer_8
  or or_4 (or_4_out, in4, in8);
  assign controlled_buffer_1_out = demultiplexer_1_out3 ? xor_1_out : 1'bz;  // Controlled_Buffer controlled_buffer_9
  xor xor_1 (xor_1_out, in1, in5);
  assign controlled_buffer_2_out = demultiplexer_1_out3 ? xor_2_out : 1'bz;  // Controlled_Buffer controlled_buffer_10
  xor xor_2 (xor_2_out, in2, in6);
  xor xor_3 (xor_3_out, in3, in7);
  assign controlled_buffer_3_out = demultiplexer_1_out3 ? xor_3_out : 1'bz;  // Controlled_Buffer controlled_buffer_11
  xor xor_4 (xor_4_out, in4, in8);
  assign controlled_buffer_1_out = demultiplexer_1_out4 ? ~in1 : 1'bz;  // Controlled_Inverter controlled_inverter_1
  assign controlled_buffer_2_out = demultiplexer_1_out4 ? ~in2 : 1'bz;  // Controlled_Inverter controlled_inverter_2
  assign controlled_buffer_3_out = demultiplexer_1_out4 ? ~in3 : 1'bz;  // Controlled_Inverter controlled_inverter_3
  not not_1 (not_1_out, demultiplexer_1_out5);
  assign controlled_buffer_4_out = demultiplexer_1_out5 ? add_1_out_10 : 1'bz;  // Controlled_Buffer controlled_buffer_12
  ADD add_1 (
    .A0(in4), .A1(in3), .A2(in2), .A3(in1), .B0(in8), .B1(in7), .B2(in6), .B3(in5), .in_1(not_1_out),
    .Overflow(Overflow), .out_10(add_1_out_10), .out_11(add_1_out_11), .out_12(add_1_out_12),
    .out_13(add_1_out_13));
  assign controlled_buffer_3_out = demultiplexer_1_out5 ? add_1_out_11 : 1'bz;  // Controlled_Buffer controlled_buffer_13
  assign controlled_buffer_2_out = demultiplexer_1_out5 ? add_1_out_12 : 1'bz;  // Controlled_Buffer controlled_buffer_14
  assign controlled_buffer_4_out = demultiplexer_1_out6 ? subs_1_out_10 : 1'bz;  // Controlled_Buffer controlled_buffer_15
  assign controlled_buffer_3_out = demultiplexer_1_out6 ? subs_1_out_11 : 1'bz;  // Controlled_Buffer controlled_buffer_16
  SUBS subs_1 (
    .A0(in4), .A1(in3), .A2(in2), .A3(in1), .B0(in8), .B1(in7), .B2(in6), .B3(in5),
    .in_2(demultiplexer_1_out6), .Overflow(Overflow_2), .out_10(subs_1_out_10), .out_11(subs_1_out_11),
    .out_12(subs_1_out_12), .out_13(subs_1_out_13));
  assign controlled_buffer_2_out = demultiplexer_1_out6 ? subs_1_out_12 : 1'bz;  // Controlled_Buffer controlled_buffer_17
  Clock reloj (.out(reloj_out));
  Demultiplexer #(.select(4)) demultiplexer_1 (
    .out1(demultiplexer_1_out1), .out2(demultiplexer_1_out2), .out3(demultiplexer_1_out3),
    .out4(demultiplexer_1_out4), .out5(demultiplexer_1_out5), .out6(demultiplexer_1_out6), .in(reloj_out),
    .sel({opcode_1, opcode_2, opcode3, opcode_4}), .en(enable_del_dmx));  // open: out0, out7, out8, out9, out10, out11, out12, out13, out14, out15
  assign controlled_buffer_4_out = demultiplexer_1_out3 ? xor_4_out : 1'bz;  // Controlled_Buffer controlled_buffer_18
  assign controlled_buffer_4_out = demultiplexer_1_out4 ? ~in4 : 1'bz;  // Controlled_Inverter controlled_inverter_4
  assign controlled_buffer_1_out = demultiplexer_1_out5 ? add_1_out_13 : 1'bz;  // Controlled_Buffer controlled_buffer_19
  assign controlled_buffer_1_out = demultiplexer_1_out6 ? subs_1_out_13 : 1'bz;  // Controlled_Buffer controlled_buffer_20
  LED output1 (.in(controlled_buffer_1_out));
  LED output2 (.in(controlled_buffer_2_out));
  LED output3 (.in(controlled_buffer_3_out));
  LED outpu4 (.in(controlled_buffer_4_out));
endmodule

module ADD (
  input  in_1,
  input  A0,
  input  A1,
  input  A2,
  input  A3,
  input  B0,
  input  B1,
  input  B2,
  input  B3,
  output out_10,
  output out_11,
  output out_12,
  output out_13,
  output Overflow
);

  wire n1_bit_adder_1_c_out, n1_bit_adder_2_c_out, n1_bit_adder_3_c_out;

  _1_bit_adder u_1_bit_adder_1 (.A(A0), .B(B0), .C_in(in_1), .C_out(n1_bit_adder_1_c_out), .Sum(out_10));
  _1_bit_adder u_1_bit_adder_2 (
    .A(A1), .B(B1), .C_in(n1_bit_adder_1_c_out), .C_out(n1_bit_adder_2_c_out), .Sum(out_11));
  _1_bit_adder u_1_bit_adder_3 (
    .A(A2), .B(B2), .C_in(n1_bit_adder_2_c_out), .C_out(n1_bit_adder_3_c_out), .Sum(out_12));
  _1_bit_adder u_1_bit_adder_4 (.A(A3), .B(B3), .C_in(n1_bit_adder_3_c_out), .C_out(Overflow), .Sum(out_13));
endmodule

module _1_bit_adder (
  input  C_in,
  input  A,
  input  B,
  output Sum,
  output C_out
);

  wire and_1_out, and_2_out, and_3_out, xor_2_out;

  and and_1 (and_1_out, C_in, A);
  and and_2 (and_2_out, C_in, B);
  and and_3 (and_3_out, A, B);
  xor xor_1 (Sum, C_in, xor_2_out);
  xor xor_2 (xor_2_out, A, B);
  or or_1 (C_out, and_1_out, and_2_out, and_3_out);
endmodule

module SUBS (
  input  A0,
  input  in_2,
  input  A1,
  input  A2,
  input  A3,
  input  B0,
  input  B1,
  input  B2,
  input  B3,
  output out_10,
  output out_11,
  output out_12,
  output out_13,
  output Overflow
);

  wire n1_bit_adder_1_c_out, n1_bit_adder_2_c_out, n1_bit_adder_3_c_out, not_1_out, not_2_out, not_3_out,
       not_4_out;

  not not_1 (not_1_out, B2);
  not not_2 (not_2_out, B0);
  not not_3 (not_3_out, B1);
  not not_4 (not_4_out, B3);
  _1_bit_adder u_1_bit_adder_1 (.A(A0), .B(not_2_out), .C_in(in_2), .C_out(n1_bit_adder_1_c_out), .Sum(out_10));
  _1_bit_adder u_1_bit_adder_2 (
    .A(A1), .B(not_3_out), .C_in(n1_bit_adder_1_c_out), .C_out(n1_bit_adder_2_c_out), .Sum(out_11));
  _1_bit_adder u_1_bit_adder_3 (
    .A(A2), .B(not_1_out), .C_in(n1_bit_adder_2_c_out), .C_out(n1_bit_adder_3_c_out), .Sum(out_12));
  _1_bit_adder u_1_bit_adder_4 (.A(A3), .B(not_4_out), .C_in(n1_bit_adder_3_c_out), .C_out(Overflow), .Sum(out_13));
endmodule
